# Fritzing sketch balance (saved by Fritzing 1.0.0d)
breadboards: 1

parts:
  L1 = Inductor [package="400 mil [THT]"]
  LED1 = smd LED [color="Infrared (940nm)" package="0603 [SMD]"]
  Q1 = LTR-301 [package=ltr-301]
  R1 = Resistor [tolerance=±5% power=0.25W resistance=200 package=THT]
  R2 = Resistor [tolerance=±5% power=0.25W resistance=200 package=THT]

nets:
  N1: L1.pin_0, R2.Pin_1
  GND: L1.pin_1, LED1.cathode
  N2: LED1.anode, Q1.C, R1.Pin_1
  SIG: Q1.E
  V3.3: R1.Pin_0
  DAC: R2.Pin_0
